// Logisim project cpu_main_circuit.circ as structural Verilog: 29 circuits, main circuit main
module main (
  input  in_1,
  input  in_2
);

  wire alu_and_mux_1_carry, bit_extractor_1_out_7, bit_extractor_2_out_7, CLK_out, cu_with_rom_1_d0,
       cu_with_rom_1_d1, cu_with_rom_1_d2, cu_with_rom_1_d3, cu_with_rom_1_d4, cu_with_rom_1_d5,
       cu_with_rom_1_d6, cu_with_rom_1_d7, cu_with_rom_1_d8, cu_with_rom_1_d9, cu_with_rom_1_d10,
       cu_with_rom_1_d11, flag_generator_1_arith_overflow, flag_generator_1_neg_less,
       flag_generator_1_zero_flg;
  wire [2:0] alu_and_mux_1_comparisn, rom_ir_pc_1_dest_res, rom_ir_pc_1_src_b, undriven;
  wire [4:0] rom_ir_pc_1_opcode;
  wire [7:0] A_B_BUFFER_out_r0, A_B_BUFFER_out_r1, ACCUMULATOR_q, alu_and_mux_1_alu_out,
       bit_extractor_1_out_07, bit_extractor_2_out_07, multiplexer_1_out, multiplexer_2_out,
       muxed_gp_res_1_data_out, rom_ir_pc_1_extra;

  Clock CLK (.out(CLK_out));
  ROM_IR_PC rom_ir_pc_1 (
    .WE_PC(cu_with_rom_1_d11), .CLK(CLK_out), .RESET(in_2), .CLEAR_IR(cu_with_rom_1_d1),
    .we_ir(cu_with_rom_1_d10), .EXTRA(rom_ir_pc_1_extra), .OPCODE(rom_ir_pc_1_opcode),
    .SRC_B(rom_ir_pc_1_src_b), .DEST_RES(rom_ir_pc_1_dest_res));
  Register ACCUMULATOR (.D(multiplexer_2_out), .en(cu_with_rom_1_d9), .clk(CLK_out), .Q(ACCUMULATOR_q), .clr(in_1));
  Multiplexer #(.width(8)) multiplexer_1 (
    .in0(ACCUMULATOR_q), .in1(rom_ir_pc_1_extra), .out(multiplexer_1_out), .sel(cu_with_rom_1_d6));
  CU_WITH_ROM cu_with_rom_1 (
    .ENB_CNTR(cu_with_rom_1_d2), .CLK(CLK_out), .COUNTER_RESET(cu_with_rom_1_d0),
    .OPCODE(rom_ir_pc_1_opcode), .D0(cu_with_rom_1_d0), .D1(cu_with_rom_1_d1), .D2(cu_with_rom_1_d2),
    .D3(cu_with_rom_1_d3), .D4(cu_with_rom_1_d4), .D5(cu_with_rom_1_d5), .D6(cu_with_rom_1_d6),
    .D7(cu_with_rom_1_d7), .D8(cu_with_rom_1_d8), .D9(cu_with_rom_1_d9), .D10(cu_with_rom_1_d10),
    .D11(cu_with_rom_1_d11));  // open: D12, D13, D14, D15
  MUXED_GP_RES muxed_gp_res_1 (
    .WE_T(cu_with_rom_1_d8), .CLK(CLK_out), .WE_SEL(rom_ir_pc_1_src_b), .DATA_IN(multiplexer_1_out),
    .SEL_RES(rom_ir_pc_1_dest_res), .DATA_OUT(muxed_gp_res_1_data_out));  // open: CLEAR_SEL
  AB_BUFFER A_B_BUFFER (
    .WE_A(cu_with_rom_1_d4), .WE_B(cu_with_rom_1_d3), .CLK(CLK_out), .IN_R0(ACCUMULATOR_q),
    .IN_R1(muxed_gp_res_1_data_out), .OUT_R0(A_B_BUFFER_out_r0), .OUT_R1(A_B_BUFFER_out_r1));  // open: RES_CLR
  BIT_EXTRACTOR bit_extractor_1 (
    .IN_07(A_B_BUFFER_out_r0), .OUT_07(bit_extractor_1_out_07), .OUT_7(bit_extractor_1_out_7));
  BIT_EXTRACTOR bit_extractor_2 (
    .IN_07(A_B_BUFFER_out_r1), .OUT_07(bit_extractor_2_out_07), .OUT_7(bit_extractor_2_out_7));
  ALU_AND_MUX alu_and_mux_1 (
    .A(bit_extractor_1_out_07), .S(undriven), .B(bit_extractor_2_out_07),
    .COMPARISN(alu_and_mux_1_comparisn), .ALU_OUT(alu_and_mux_1_alu_out), .CARRY(alu_and_mux_1_carry));
  Multiplexer #(.width(8)) multiplexer_2 (
    .in0(alu_and_mux_1_alu_out), .in1(bit_extractor_2_out_07), .out(multiplexer_2_out), .sel(cu_with_rom_1_d5));
  FLAG_GENERATOR flag_generator_1 (
    .RESULT_IN(multiplexer_2_out), .A7_IN(bit_extractor_1_out_7), .B7_IN(bit_extractor_2_out_7),
    .COMPARATOR_IN(alu_and_mux_1_comparisn), .ZERO_FLG(flag_generator_1_zero_flg),
    .NEG_LESS(flag_generator_1_neg_less), .ARITH_OVERFLOW(flag_generator_1_arith_overflow));
  FLG_RESISTER flg_resister_1 (
    .FLG_0(flag_generator_1_zero_flg), .FLG_1(flag_generator_1_neg_less),
    .FLG_2(flag_generator_1_arith_overflow), .FLG_3(alu_and_mux_1_carry), .WE_FLG(cu_with_rom_1_d7),
    .CLK(CLK_out));  // open: CLR_FLG, FLG_O0, FLG_O1, FLG_O2, FLG_O3
endmodule

module FULL_ADDER (
  input  Cin,
  input  A,
  input  B,
  output S,
  output Cout
);

  wire and_1_out, and_2_out, xor_1_out;

  xor xor_1 (xor_1_out, A, B);
  and and_1 (and_1_out, B, A);
  xor xor_2 (S, Cin, xor_1_out);
  and and_2 (and_2_out, xor_1_out, Cin);
  or or_1 (Cout, and_2_out, and_1_out);
endmodule

module ADD_SUBS (
  input  M,
  input  [7:0] B,
  input  [7:0] A,
  output [7:0] S,
  output Cout
);

  wire full_adder_1_cout, full_adder_2_cout, full_adder_3_cout, full_adder_4_cout, full_adder_5_cout,
       full_adder_6_cout, full_adder_7_cout, xor_1_out, xor_2_out, xor_3_out, xor_4_out, xor_5_out,
       xor_6_out, xor_7_out, xor_8_out;

  xor xor_1 (xor_1_out, M, B[0]);
  FULL_ADDER full_adder_1 (.Cin(M), .A(A[0]), .B(xor_1_out), .S(S[0]), .Cout(full_adder_1_cout));
  xor xor_2 (xor_2_out, M, B[1]);
  FULL_ADDER full_adder_2 (.Cin(full_adder_1_cout), .A(A[1]), .B(xor_2_out), .S(S[1]), .Cout(full_adder_2_cout));
  xor xor_3 (xor_3_out, M, B[2]);
  FULL_ADDER full_adder_3 (.Cin(full_adder_2_cout), .A(A[2]), .B(xor_3_out), .S(S[2]), .Cout(full_adder_3_cout));
  xor xor_4 (xor_4_out, M, B[3]);
  FULL_ADDER full_adder_4 (.Cin(full_adder_3_cout), .A(A[3]), .B(xor_4_out), .S(S[3]), .Cout(full_adder_4_cout));
  FULL_ADDER full_adder_5 (.Cin(full_adder_4_cout), .A(A[4]), .B(xor_5_out), .S(S[4]), .Cout(full_adder_5_cout));
  xor xor_5 (xor_5_out, M, B[4]);
  FULL_ADDER full_adder_6 (.Cin(full_adder_5_cout), .A(A[5]), .B(xor_6_out), .S(S[5]), .Cout(full_adder_6_cout));
  xor xor_6 (xor_6_out, M, B[5]);
  FULL_ADDER full_adder_7 (.Cin(full_adder_6_cout), .A(A[6]), .B(xor_7_out), .S(S[6]), .Cout(full_adder_7_cout));
  xor xor_7 (xor_7_out, M, B[6]);
  FULL_ADDER full_adder_8 (.Cin(full_adder_7_cout), .A(A[7]), .B(xor_8_out), .S(S[7]), .Cout(Cout));
  xor xor_8 (xor_8_out, M, B[7]);
endmodule

module MUX_4X1 (
  input  I3,
  input  I2,
  input  I1,
  input  I0,
  input  S0,
  input  S1,
  output Y
);

  wire and_1_out, and_2_out, and_3_out, and_4_out, not_1_out, not_2_out;

  not not_1 (not_1_out, S0);
  and and_1 (and_1_out, I3, S0, S1);
  and and_2 (and_2_out, I2, S0, not_2_out);
  and and_3 (and_3_out, I1, S1, not_1_out);
  and and_4 (and_4_out, I0, not_1_out, not_2_out);
  not not_2 (not_2_out, S1);
  or or_1 (Y, and_1_out, and_2_out, and_3_out, and_4_out);
endmodule

module MUX_8BIT (
  input  S1,
  input  S0,
  input  [7:0] L_AND,
  input  [7:0] L_OR,
  input  [7:0] SUBS,
  input  [7:0] ADD,
  output [7:0] Y
);

  MUX_4X1 mux_4x1_1 (.I3(ADD[7]), .I2(SUBS[7]), .I1(L_OR[7]), .I0(L_AND[7]), .S0(S0), .S1(S1), .Y(Y[7]));
  MUX_4X1 mux_4x1_2 (.I3(ADD[6]), .I2(SUBS[6]), .I1(L_OR[6]), .I0(L_AND[6]), .S0(S0), .S1(S1), .Y(Y[6]));
  MUX_4X1 mux_4x1_3 (.I3(ADD[5]), .I2(SUBS[5]), .I1(L_OR[5]), .I0(L_AND[5]), .S0(S0), .S1(S1), .Y(Y[5]));
  MUX_4X1 mux_4x1_4 (.I3(ADD[4]), .I2(SUBS[4]), .I1(L_OR[4]), .I0(L_AND[4]), .S0(S0), .S1(S1), .Y(Y[4]));
  MUX_4X1 mux_4x1_5 (.I3(ADD[3]), .I2(SUBS[3]), .I1(L_OR[3]), .I0(L_AND[3]), .S0(S0), .S1(S1), .Y(Y[3]));
  MUX_4X1 mux_4x1_6 (.I3(ADD[2]), .I2(SUBS[2]), .I1(L_OR[2]), .I0(L_AND[2]), .S0(S0), .S1(S1), .Y(Y[2]));
  MUX_4X1 mux_4x1_7 (.I3(ADD[1]), .I2(SUBS[1]), .I1(L_OR[1]), .I0(L_AND[1]), .S0(S0), .S1(S1), .Y(Y[1]));
  MUX_4X1 mux_4x1_8 (.I3(ADD[0]), .I2(SUBS[0]), .I1(L_OR[0]), .I0(L_AND[0]), .S0(S0), .S1(S1), .Y(Y[0]));
endmodule

module OR_1BIT (
  input  in_1,
  input  in_2,
  output out_3
);

  or or_1 (out_3, in_1, in_2);
endmodule

module OR_8BIT (
  input  [7:0] A,
  input  [7:0] B,
  output [7:0] Y
);

  or or_1 (Y[0], A[0], B[0]);
  or or_2 (Y[1], A[1], B[1]);
  or or_3 (Y[2], A[2], B[2]);
  or or_4 (Y[3], A[3], B[3]);
  or or_5 (Y[4], A[4], B[4]);
  or or_6 (Y[5], A[5], B[5]);
  or or_7 (Y[6], A[6], B[6]);
  or or_8 (Y[7], A[7], B[7]);
endmodule

module AND_1BIT (
  input  in_1,
  input  in_2,
  output out_3
);

  and and_1 (out_3, in_1, in_2);
endmodule

module AND_8BIT (
  input  [7:0] A,
  input  [7:0] B,
  output [7:0] Y
);

  and and_1 (Y[0], A[0], B[0]);
  and and_2 (Y[1], A[1], B[1]);
  and and_3 (Y[2], A[2], B[2]);
  and and_4 (Y[3], A[3], B[3]);
  and and_5 (Y[4], A[4], B[4]);
  and and_6 (Y[5], A[5], B[5]);
  and and_7 (Y[6], A[6], B[6]);
  and and_8 (Y[7], A[7], B[7]);
endmodule

module TEST (
  input  B7,
  input  A7,
  input  B6,
  input  A6,
  input  B5,
  input  A5,
  input  B4,
  input  A4,
  input  B3,
  input  A3,
  input  B2,
  input  A2,
  input  in_13,
  input  B1,
  input  A1,
  input  B0,
  input  A0,
  input  A,
  input  B,
  input  in_20,
  input  in_21,
  output S7,
  output S6,
  output S5,
  output S4,
  output S3,
  output S2,
  output S1,
  output S0,
  output out_30,
  output out_31
);

  wire AND_1_out_3, F_ADDER_s, full_adder_1_cout, full_adder_2_cout, full_adder_3_cout, full_adder_4_cout,
       full_adder_5_cout, full_adder_6_cout, full_adder_7_cout, OR_1_out_3, xor_1_out, xor_2_out, xor_3_out,
       xor_4_out, xor_5_out, xor_6_out, xor_7_out, xor_8_out;

  xor xor_1 (xor_1_out, in_13, B7);
  FULL_ADDER full_adder_1 (.Cin(in_13), .A(A7), .B(xor_1_out), .S(S0), .Cout(full_adder_1_cout));
  xor xor_2 (xor_2_out, in_13, B6);
  FULL_ADDER full_adder_2 (.Cin(full_adder_1_cout), .A(A6), .B(xor_2_out), .S(S1), .Cout(full_adder_2_cout));
  xor xor_3 (xor_3_out, in_13, B5);
  FULL_ADDER full_adder_3 (.Cin(full_adder_2_cout), .A(A5), .B(xor_3_out), .S(S2), .Cout(full_adder_3_cout));
  xor xor_4 (xor_4_out, in_13, B4);
  FULL_ADDER full_adder_4 (.Cin(full_adder_3_cout), .A(A4), .B(xor_4_out), .S(S3), .Cout(full_adder_4_cout));
  FULL_ADDER F_ADDER (.A(A), .B(B), .S(F_ADDER_s));  // open: Cin, Cout
  OR_1BIT OR_1 (.in_1(A), .in_2(B), .out_3(OR_1_out_3));
  AND_1BIT AND_1 (.in_1(A), .in_2(B), .out_3(AND_1_out_3));
  FULL_ADDER full_adder_5 (.Cin(full_adder_4_cout), .A(A3), .B(xor_5_out), .S(S4), .Cout(full_adder_5_cout));
  xor xor_5 (xor_5_out, in_13, B3);
  MUX_4X1 MUX_4X2 (.I3(F_ADDER_s), .I1(OR_1_out_3), .I0(AND_1_out_3), .S0(in_20), .S1(in_21), .Y(out_31));  // open: I2
  FULL_ADDER full_adder_6 (.Cin(full_adder_5_cout), .A(A2), .B(xor_6_out), .S(S5), .Cout(full_adder_6_cout));
  xor xor_6 (xor_6_out, in_13, B2);
  FULL_ADDER full_adder_7 (.Cin(full_adder_6_cout), .A(A1), .B(xor_7_out), .S(S6), .Cout(full_adder_7_cout));
  xor xor_7 (xor_7_out, in_13, B1);
  FULL_ADDER full_adder_8 (.Cin(full_adder_7_cout), .A(A0), .B(xor_8_out), .S(S7), .Cout(out_30));
  xor xor_8 (xor_8_out, in_13, B0);
endmodule

// ALU_WT_MUX
module ALU_AND_MUX (
  input  [7:0] A,
  input  [7:0] B,
  input  [2:0] S,
  output CARRY,
  output [7:0] ALU_OUT,
  output [2:0] COMPARISN
);

  wire adder_1_cout, adder_2_cout, not_2_out;
  wire [7:0] adder_1_out, adder_2_out, and_1_out, not_1_out, or_1_out, shifter_1_out, shifter_2_out,
       shifter_3_out;

  assign not_1_out = ~B;  // NOT_Gate not_1, 8 bits wide
  assign or_1_out = A | B;  // OR_Gate or_1, 8 bits wide
  assign and_1_out = A & B;  // AND_Gate and_1, 8 bits wide
  Adder adder_1 (.a(A), .b(B), .out(adder_1_out), .cout(adder_1_cout));  // open: cin
  Adder adder_2 (.a(A), .b(not_1_out), .out(adder_2_out), .cin(1'b1), .cout(adder_2_cout));
  not not_2 (not_2_out, adder_2_cout);
  Shifter shifter_1 (.in(A), .\dist (3'b001), .out(shifter_1_out));
  Shifter #(.shift("ar")) shifter_2 (.in(A), .\dist (3'b001), .out(shifter_2_out));
  Shifter #(.shift("rr")) shifter_3 (.in(A), .\dist (3'b001), .out(shifter_3_out));
  Comparator comparator_1 (.a(A), .b(B), .gt(COMPARISN[0]), .eq(COMPARISN[1]), .lt(COMPARISN[2]));
  or or_2 (CARRY, adder_1_cout, not_2_out);
  Multiplexer #(.select(3), .width(8)) multiplexer_1 (
    .in0(adder_1_out), .in1(adder_2_out), .in2(or_1_out), .in3(and_1_out), .in4(shifter_1_out),
    .in5(shifter_2_out), .in6(shifter_3_out), .out(ALU_OUT), .sel(S));  // open: in7
endmodule

// GP_RESISTER
module GP_RES (
  input  [7:0] IN_RES,
  input  WE_T,
  input  [2:0] WE_SEL,
  input  [7:0] CLR_SEL,
  input  CLK,
  output [7:0] OUT_R0,
  output [7:0] OUT_R1,
  output [7:0] OUT_R2,
  output [7:0] OUT_R3,
  output [7:0] OUT_R4,
  output [7:0] OUT_R5,
  output [7:0] OUT_R6,
  output [7:0] OUT_R7
);

  wire [7:0] gp_resister_mux_1_we_selected_resister;

  GP_RESISTER_MUX gp_resister_mux_1 (
    .WE_T(WE_T), .WE_SEL(WE_SEL), .WE_SELECTED_RESISTER(gp_resister_mux_1_we_selected_resister));
  Register register_1 (
    .D(IN_RES), .en(gp_resister_mux_1_we_selected_resister[0]), .clk(CLK), .Q(OUT_R0), .clr(CLR_SEL[0]));
  Register register_2 (
    .D(IN_RES), .en(gp_resister_mux_1_we_selected_resister[1]), .clk(CLK), .Q(OUT_R1), .clr(CLR_SEL[1]));
  Register register_3 (
    .D(IN_RES), .en(gp_resister_mux_1_we_selected_resister[2]), .clk(CLK), .Q(OUT_R2), .clr(CLR_SEL[2]));
  Register register_4 (
    .D(IN_RES), .en(gp_resister_mux_1_we_selected_resister[3]), .clk(CLK), .Q(OUT_R3), .clr(CLR_SEL[3]));
  Register register_5 (
    .D(IN_RES), .en(gp_resister_mux_1_we_selected_resister[4]), .clk(CLK), .Q(OUT_R4), .clr(CLR_SEL[4]));
  Register register_6 (
    .D(IN_RES), .en(gp_resister_mux_1_we_selected_resister[5]), .clk(CLK), .Q(OUT_R5), .clr(CLR_SEL[5]));
  Register register_7 (
    .D(IN_RES), .en(gp_resister_mux_1_we_selected_resister[6]), .clk(CLK), .Q(OUT_R6), .clr(CLR_SEL[6]));
  Register register_8 (
    .D(IN_RES), .en(gp_resister_mux_1_we_selected_resister[7]), .clk(CLK), .Q(OUT_R7), .clr(CLR_SEL[7]));
endmodule

module SP_RES (
  input  [7:0] IN_R0,
  input  WE_R0,
  input  R0_CLR,
  input  [7:0] IN_R1,
  input  WE_R1,
  input  R1_CLR,
  input  [7:0] IN_R2,
  input  WE_R2,
  input  R2_CLR,
  input  CLK,
  output [7:0] OUT_R0,
  output [7:0] OUT_R1,
  output [7:0] OUT_R2
);

  Register register_1 (.D(IN_R0), .en(WE_R0), .clk(CLK), .Q(OUT_R0), .clr(R0_CLR));
  Register register_2 (.D(IN_R1), .en(WE_R1), .clk(CLK), .Q(OUT_R1), .clr(R1_CLR));
  Register register_3 (.D(IN_R2), .en(WE_R2), .clk(CLK), .Q(OUT_R2), .clr(R2_CLR));
endmodule

module TME_GEN (
  input  LD,
  input  [2:0] DATA,
  input  ENB,
  input  CLK,
  output [7:0] T
);

  wire and_1_out, not_1_out, not_2_out;
  wire [2:0] counter_1_q;

  Counter #(.max('h7), .width(3)) counter_1 (
    .load(LD), .D(DATA), .count(ENB), .Q(counter_1_q), .clk(CLK), .clr(and_1_out));  // open: carry, up
  and and_1 (and_1_out, not_1_out, not_2_out, counter_1_q[2]);
  not not_1 (not_1_out, counter_1_q[0]);
  not not_2 (not_2_out, counter_1_q[1]);
  Decoder #(.enable("false"), .select(3)) decoder_1 (
    .out0(T[0]), .out1(T[1]), .out2(T[2]), .out3(T[3]), .out4(T[4]), .out5(T[5]), .out6(T[6]), .out7(T[7]),
    .sel(counter_1_q));
endmodule

module CTRL_AND (
  input  T,
  input  INIT_MODE,
  output OP
);

  wire not_1_out;

  not not_1 (not_1_out, INIT_MODE);
  and and_1 (OP, T, not_1_out);
endmodule

module AB_BUFFER (
  input  [7:0] IN_R0,
  input  WE_A,
  input  [7:0] IN_R1,
  input  WE_B,
  input  RES_CLR,
  input  CLK,
  output [7:0] OUT_R0,
  output [7:0] OUT_R1
);

  Register register_1 (.D(IN_R0), .en(WE_A), .clk(CLK), .Q(OUT_R0));  // open: clr
  Register register_2 (.D(IN_R1), .en(WE_B), .clk(CLK), .Q(OUT_R1), .clr(RES_CLR));
endmodule

module CU (
  input  [7:0] INSTRUCTION_IN,
  input  WE_INSTRUCTION,
  input  IR_RESET,
  input  INIT_MODE,
  input  CLK,
  output [1:0] SELECT_A,
  output [1:0] SELECT_B,
  output [1:0] WE_SEL,
  output T0,
  output T1,
  output ALU_MD,
  output T2,
  output MOV_MD,
  output T3,
  output CLR_MD,
  output RESERVED_MD
);

  wire not_1_out, or_1_out;
  wire [7:4] COUNTER_t;
  wire [7:6] IR_q;

  not not_1 (not_1_out, WE_INSTRUCTION);
  or or_1 (or_1_out, INIT_MODE, not_1_out);
  Register IR (
    .D(INSTRUCTION_IN), .en(WE_INSTRUCTION), .clk(CLK), .Q({IR_q, WE_SEL, SELECT_B, SELECT_A}), .clr(IR_RESET));
  TME_GEN COUNTER (.LD(INIT_MODE), .ENB(or_1_out), .CLK(CLK), .DATA(3'b011), .T({COUNTER_t, T3, T2, T1, T0}));
  Decoder #(.enable("false"), .select(2)) decoder_1 (
    .out0(ALU_MD), .out1(MOV_MD), .out2(CLR_MD), .out3(RESERVED_MD), .sel(IR_q));

  // Notes on the sheet:
  //   OPCODE
endmodule

module TESING_UNT (
  input  [2:0] MAN_DATA_TO_COUNTER,
  input  LOAD_MAN_DATA_TO_COUNTER,
  input  [15:0] in_3,
  input  in_4,
  input  [2:0] in_5,
  input  LD,
  input  [2:0] DATA,
  input  ENB,
  input  CLK,
  input  ENB_CNTR,
  output T4,
  output T5,
  output [3:0] INS_OUT,
  output T6,
  output T7,
  output [2:0] RESERVED,
  output [2:0] SEL_RES_B,
  output [2:0] SEL_RES_A,
  output [2:0] DEST_RES_SEL,
  output [7:0] DATA_OUT,
  output T0,
  output T1,
  output T2,
  output T3,
  output out_25,
  output out_26,
  output out_27,
  output out_28
);

  wire [1:0] undriven;
  wire [2:0] counter_1_q, undriven_2;

  Demultiplexer #(.select(2)) demultiplexer_1 (
    .out0(INS_OUT[0]), .out1(INS_OUT[1]), .out2(INS_OUT[2]), .out3(INS_OUT[3]), .sel(undriven));  // open: in
  Counter #(.max('h7), .width(3)) counter_1 (
    .load(LD), .D(DATA), .count(ENB), .Q(counter_1_q), .clk(CLK));  // open: carry, up, clr
  Decoder #(.enable("false"), .select(3)) decoder_1 (
    .out0(T0), .out1(T1), .out2(T2), .out3(T3), .out4(out_25), .out5(out_26), .out6(out_27), .out7(out_28),
    .sel(undriven_2));
  ROM rom_1 (.addr({1'b0, in_3[15:12], counter_1_q}), .data(DATA_OUT));

  assign DEST_RES_SEL = in_3[11:9];
  assign RESERVED = in_3[2:0];
  assign SEL_RES_A = in_3[8:6];
  assign SEL_RES_B = in_3[5:3];

  // Notes on the sheet:
  //   SEL_A
  //   SEL_A
  //   RES_SEL
  //   ALU
  //   SEL_A
  //   SEL_A
  //   RES_SEL
  //   ALU
endmodule

// GP_RES_MUX
module B_RESISTER_SELECTOR (
  input  [7:0] R0,
  input  [7:0] R1,
  input  [7:0] R2,
  input  [7:0] R3,
  input  [7:0] R4,
  input  [7:0] R5,
  input  [7:0] R6,
  input  [7:0] R7,
  input  [2:0] SEL_B,
  output [7:0] SELECTED_B
);

  Multiplexer #(.select(3), .width(8)) multiplexer_1 (
    .in0(R0), .in1(R1), .in2(R2), .in3(R3), .in4(R4), .in5(R5), .in6(R6), .in7(R7), .out(SELECTED_B),
    .sel(SEL_B));
endmodule

module GP_RESISTER_MUX (
  input  WE_T,
  input  [2:0] WE_SEL,
  output [7:0] WE_SELECTED_RESISTER
);

  Demultiplexer #(.select(3)) demultiplexer_1 (
    .out0(WE_SELECTED_RESISTER[0]), .out1(WE_SELECTED_RESISTER[1]), .out2(WE_SELECTED_RESISTER[2]),
    .out3(WE_SELECTED_RESISTER[3]), .out4(WE_SELECTED_RESISTER[4]), .out5(WE_SELECTED_RESISTER[5]),
    .out6(WE_SELECTED_RESISTER[6]), .out7(WE_SELECTED_RESISTER[7]), .in(WE_T), .sel(WE_SEL));
endmodule

// CONTROL_UNIT
module CU_WITH_ROM (
  input  [4:0] OPCODE,
  input  ENB_CNTR,
  input  CLK,
  input  COUNTER_RESET,
  output D0,
  output D1,
  output D2,
  output D3,
  output D4,
  output D5,
  output D6,
  output D7,
  output D8,
  output D9,
  output D10,
  output D11,
  output D12,
  output D13,
  output D14,
  output D15
);

  wire [3:0] counter_1_q;

  ROM #(.addrWidth(9), .dataWidth(16)) rom_1 (
    .addr({OPCODE, counter_1_q}),
    .data({D15, D14, D13, D12, D11, D10, D9, D8, D7, D6, D5, D4, D3, D2, D1, D0}));
  Counter #(.max('hf), .width(4)) counter_1 (
    .count(ENB_CNTR), .Q(counter_1_q), .clk(CLK), .clr(COUNTER_RESET));  // open: load, D, carry, up

  // Notes on the sheet:
  //   contents of rom_1 (hex, n*v repeats v):
  //   1804 144 144 1005 12*0 1804 2c 224 1005 7*0 1000 4*0 1804 1c 204 1005 1000 11*0 1804 201c 2204 1005
  //   12*0 1804 401c 4204 1005 12*0 1804 601c 6204 1005 12*0 1804 8014 8204 1005 12*0 1804 a014 a204 1005
  //   12*0 1804 c014 c204 1005 12*0 1804 2114 210c 2204 1005 11*0 1804 1c 84 1 12*0 1804 1c04 1005
endmodule

// RESISTER_8BIT
module UNIT_RESISTER (
  input  [7:0] IN_RES,
  input  WE_RES,
  input  CLK,
  input  RESET_DATA,
  output [7:0] DATA_OUT
);

  Register register_1 (.D(IN_RES), .en(WE_RES), .clk(CLK), .Q(DATA_OUT), .clr(RESET_DATA));
endmodule

// TAP7
module BIT_EXTRACTOR (
  input  [7:0] IN_07,
  output OUT_7,
  output [7:0] OUT_07
);


  assign OUT_07 = IN_07;
  assign OUT_7 = IN_07[7];
endmodule

// FLAG_GEN
module FLAG_GENERATOR (
  input  A7_IN,
  input  [7:0] RESULT_IN,
  input  B7_IN,
  input  [2:0] COMPARATOR_IN,
  output ARITH_OVERFLOW,
  output ZERO_FLG,
  output NEG_LESS
);

  wire and_1_out, and_2_out, and_3_out, not_1_out, not_2_out, not_3_out, not_4_out;

  and and_1 (and_1_out, RESULT_IN[0], RESULT_IN[1], RESULT_IN[2], RESULT_IN[3], RESULT_IN[4], RESULT_IN[5], RESULT_IN[6], RESULT_IN[7]);
  not not_1 (not_1_out, and_1_out);
  or or_1 (ZERO_FLG, not_1_out, COMPARATOR_IN[1]);
  not not_2 (not_2_out, RESULT_IN[7]);
  not not_3 (not_3_out, A7_IN);
  not not_4 (not_4_out, B7_IN);
  and and_2 (and_2_out, A7_IN, B7_IN, not_2_out);
  or or_2 (ARITH_OVERFLOW, and_2_out, and_3_out);
  and and_3 (and_3_out, not_3_out, not_4_out, RESULT_IN[7]);
  or or_3 (NEG_LESS, RESULT_IN[7], COMPARATOR_IN[2]);
endmodule

module FLAG_RES (
  input  FI_R0,
  input  FI_R1,
  input  FI_R2,
  input  FI_R3,
  input  WE_FLAG,
  input  CLK,
  input  RESET_FLAG_RES,
  output FO_R0,
  output FO_R1,
  output FO_R2,
  output FO_R3
);

  Register #(.width(4)) register_1 (
    .D({FI_R3, FI_R2, FI_R1, FI_R0}), .en(WE_FLAG), .clk(CLK), .Q({FO_R3, FO_R2, FO_R1, FO_R0}),
    .clr(RESET_FLAG_RES));
endmodule

// GPR_ND_MUX
module MUXED_GP_RES (
  input  [7:0] DATA_IN,
  input  WE_T,
  input  [2:0] WE_SEL,
  input  [7:0] CLEAR_SEL,
  input  CLK,
  input  [2:0] SEL_RES,
  output [7:0] DATA_OUT
);

  wire [7:0] gp_res_1_out_r0, gp_res_1_out_r1, gp_res_1_out_r2, gp_res_1_out_r3, gp_res_1_out_r4,
       gp_res_1_out_r5, gp_res_1_out_r6, gp_res_1_out_r7;

  GP_RES gp_res_1 (
    .WE_T(WE_T), .CLK(CLK), .WE_SEL(WE_SEL), .IN_RES(DATA_IN), .CLR_SEL(CLEAR_SEL), .OUT_R0(gp_res_1_out_r0),
    .OUT_R1(gp_res_1_out_r1), .OUT_R2(gp_res_1_out_r2), .OUT_R3(gp_res_1_out_r3), .OUT_R4(gp_res_1_out_r4),
    .OUT_R5(gp_res_1_out_r5), .OUT_R6(gp_res_1_out_r6), .OUT_R7(gp_res_1_out_r7));
  B_RESISTER_SELECTOR b_resister_selector_1 (
    .R0(gp_res_1_out_r0), .R1(gp_res_1_out_r1), .R2(gp_res_1_out_r2), .R3(gp_res_1_out_r3),
    .R4(gp_res_1_out_r4), .R5(gp_res_1_out_r5), .R6(gp_res_1_out_r6), .R7(gp_res_1_out_r7), .SEL_B(SEL_RES),
    .SELECTED_B(DATA_OUT));
endmodule

// FLG_REG
module FLG_RESISTER (
  input  FLG_0,
  input  FLG_1,
  input  FLG_2,
  input  FLG_3,
  input  WE_FLG,
  input  CLK,
  input  CLR_FLG,
  output FLG_O0,
  output FLG_O1,
  output FLG_O2,
  output FLG_O3
);

  Register #(.width(4)) register_1 (
    .D({FLG_3, FLG_2, FLG_1, FLG_0}), .en(WE_FLG), .clk(CLK), .Q({FLG_O3, FLG_O2, FLG_O1, FLG_O0}),
    .clr(CLR_FLG));
endmodule

// PC
module PROGRAM_COUNTER (
  input  [4:0] NEW_ADDR,
  input  JUMP_OTHERS,
  input  WE_PC,
  input  CLK,
  input  RESET,
  output [4:0] CURRENT_ADDR
);

  wire [4:0] adder_1_out, multiplexer_1_out;

  Multiplexer #(.width(5)) multiplexer_1 (
    .in0(adder_1_out), .in1(NEW_ADDR), .out(multiplexer_1_out), .sel(JUMP_OTHERS));
  Register #(.width(5)) register_1 (.D(multiplexer_1_out), .en(WE_PC), .clk(CLK), .Q(CURRENT_ADDR), .clr(RESET));
  Adder #(.width(5)) adder_1 (.a(CURRENT_ADDR), .b(5'b00001), .out(adder_1_out), .cin(1'b0));  // open: cout
endmodule

// PC_INS_IR
module ROM_IR_PC (
  input  WE_PC,
  input  CLK,
  input  RESET,
  input  CLEAR_IR,
  input  we_ir,
  output [7:0] EXTRA,
  output [2:0] SRC_B,
  output [2:0] DEST_RES,
  output [4:0] OPCODE
);

  wire nor_1_out, not_1_out, not_2_out, not_3_out, or_1_out;
  wire [4:0] program_counter_1_current_addr;
  wire [7:5] register_1_q;
  wire [15:0] rom_1_data;

  ROM #(.addrWidth(5), .dataWidth(16)) rom_1 (.addr(program_counter_1_current_addr), .data(rom_1_data));
  PROGRAM_COUNTER program_counter_1 (
    .NEW_ADDR(EXTRA[4:0]), .JUMP_OTHERS(nor_1_out), .WE_PC(WE_PC), .CLK(CLK), .RESET(RESET),
    .CURRENT_ADDR(program_counter_1_current_addr));
  Register #(.width(16)) register_1 (
    .D(rom_1_data), .en(we_ir), .clk(CLK), .Q({OPCODE, DEST_RES, register_1_q, EXTRA[4:0]}), .clr(CLEAR_IR));
  Demultiplexer #(.width(3)) demultiplexer_1 (.out0(EXTRA[7:5]), .out1(SRC_B), .in(register_1_q), .sel(or_1_out));
  not not_1 (not_1_out, OPCODE[0]);
  not not_2 (not_2_out, OPCODE[1]);
  not not_3 (not_3_out, OPCODE[3]);
  or or_1 (or_1_out, OPCODE[0], OPCODE[1], OPCODE[2], OPCODE[3], OPCODE[4]);
  nor nor_1 (nor_1_out, not_1_out, not_2_out, OPCODE[2], not_3_out, OPCODE[4]);

  // Notes on the sheet:
  //   contents of rom_1 (hex, n*v repeats v):
  //   4b 7b 820 1120 1920 2120 2920 3000 2800 4000 5806
endmodule
